# Fritzing sketch f1 (saved by Fritzing 0.9.4)
breadboards: 1

parts:
  Mod1 = Raspberry Pi Pico
  U1 = POT [package=pot_alpha_rv16af-20]
  M1 = Dagu DGServo 9g (Top view) [part_number=RS001B]

nets:
  N1: Mod1.pin_1, M1.pulse
  N2: Mod1.pin_3, Mod1.pin_8, Mod1.pin_13, Mod1.pin_18, Mod1.pin_23, Mod1.pin_28, Mod1.pin_33, Mod1.pin_38, Mod1.pin_42, M1.gnd
  N3: Mod1.pin_32, U1.E
  N4: Mod1.pin_34, U1.S
  N5: Mod1.pin_36, U1.A
  N6: Mod1.pin_40, M1.vcc

custom parts:
  Raspberry Pi Pico: Raspberry Pi Pico. Based around the RP2040 microcontroller the Pico is a low cost microcontroller device bringing Raspberry Pi quality, cost, and easy of use to the microcontroller space. Jan 2021, Split part in to two versions: tht (this one) and SMD. This one will drill holes for a .1 in header in pcb to allow plugging in the module as well as providing pads to solder the module to the top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
