# Fritzing sketch f2 (saved by Fritzing 0.9.4)
breadboards: 1

parts:
  Mod1 = Raspberry Pi Pico
  U1 = POT [package=pot_alpha_rv16af-20]
  R1 = Resistor [tolerance=±5% resistance=220 package=THT]
  LED1 = RGB LED (com. anode, rbg) [package="5 mm [THT]"]
  R2 = Photocell (LDR) [package=THT]
  J1 = Piezo Speaker
  S1 = Pushbutton [package="[THT]"]
  R3 = Resistor [tolerance=±5% resistance=220 package=THT]
  DI1 = 7-Segment LED Display [package=THT]
  M1 = Dagu DGServo 9g (Top view) [part_number=RS001B]

nets:
  N1: Mod1.pin_1, M1.pulse
  N2: Mod1.pin_3, Mod1.pin_8, Mod1.pin_13, Mod1.pin_18, Mod1.pin_23, Mod1.pin_28, Mod1.pin_33, Mod1.pin_38, Mod1.pin_42, R1.Pin_0, R2.pin_0, J1.pin1, M1.gnd
  N3: Mod1.pin_4, DI1.cathodeG
  N4: Mod1.pin_5, DI1.cathodeF
  N5: Mod1.pin_6, DI1.cathodeA
  N6: Mod1.pin_7, DI1.cathodeB
  N7: Mod1.pin_9, DI1.cathodeE
  N8: Mod1.pin_10, DI1.cathodeD
  N9: Mod1.pin_11, DI1.cathodeC
  N10: Mod1.pin_12, S1.Pin_1, S1.Pin_2
  N11: Mod1.pin_14, LED1.green_cathode
  N12: Mod1.pin_15, LED1.blue_cathode
  N13: Mod1.pin_16, LED1.common_anode
  N14: Mod1.pin_17, LED1.red_cathode
  N15: Mod1.pin_20, J1.pin2
  N16: Mod1.pin_31, R2.pin_1, R3.Pin_1
  N17: Mod1.pin_32, U1.E
  N18: Mod1.pin_34, U1.S
  N19: Mod1.pin_36, U1.A, R3.Pin_0
  N20: Mod1.pin_40, M1.vcc
  N21: R1.Pin_1, DI1.commAnode#7
  N22: S1.Pin_3, S1.Pin_4

custom parts:
  Raspberry Pi Pico: Raspberry Pi Pico. Based around the RP2040 microcontroller the Pico is a low cost microcontroller device bringing Raspberry Pi quality, cost, and easy of use to the microcontroller space. Jan 2021, Split part in to two versions: tht (this one) and SMD. This one will drill holes for a .1 in header in pcb to allow plugging in the module as well as providing pads to solder the module to the top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
