# Fritzing sketch f3 (saved by Fritzing 0.9.4)
breadboards: 1

parts:
  Part1 = Arduino Nano (Rev3.0)
  M1 = Dagu DGServo 9g (Top view) [part_number=RS001B]
  J1 = Piezo Speaker
  S1 = Pushbutton [package="[SMD]"]
  R1 = Photocell (LDR) [package=THT]
  R2 = Resistor [tolerance=±5% resistance=10k package=THT]
  U1 = POT [package=pot_alpha_rv16af-20]
  LED1 = RGB LED (com. anode, rbg) [package="5 mm [THT]"]
  7_Segment1 = 7-Segment LED Display [package=THT]
  R3 = Resistor [tolerance=±5% resistance=220 package=THT]

nets:
  N1: Part1.D0/RX, S1.Pin_1, S1.Pin_2
  GND: Part1.GND, M1.gnd, R2.Pin_0, U1.E, R3.Pin_0
  N2: Part1.D2, 7_Segment1.cathodeA
  N3: Part1.D3, 7_Segment1.cathodeB
  N4: Part1.D4, 7_Segment1.cathodeC
  N5: Part1.D5, LED1.red_cathode
  N6: Part1.D6, LED1.blue_cathode
  N7: Part1.D7, 7_Segment1.cathodeE
  N8: Part1.D8, 7_Segment1.cathodeD
  N9: Part1.D9, LED1.green_cathode
  N10: Part1.D10, M1.pulse
  N11: Part1.D11/MOSI, J1.pin2
  N12: Part1.D12/MISO, 7_Segment1.cathodeF
  5V: Part1.5V, M1.vcc
  N13: Part1.A1, R1.pin_1, R2.Pin_1
  N14: Part1.A0, U1.S
  N15: Part1.3V3, S1.Pin_3, S1.Pin_4, R1.pin_0, U1.A, LED1.common_anode
  N16: Part1.D13/SCK, 7_Segment1.cathodeG
  N17: J1.pin1, 7_Segment1.commAnode#7, R3.Pin_1
