# Fritzing sketch p2 (saved by Fritzing 0.9.4)
breadboards: 1

parts:
  R1 = Resistor [tolerance=±5% resistance=220 package=THT]
  LED1 = RGB LED (com. cathode, rgb) [package="5 mm [THT]"]
  Mod1 = Raspberry Pi Pico

nets:
  N1: R1.Pin_0, Mod1.pin_19
  N2: R1.Pin_1, LED1.common_cathode
  N3: LED1.red_anode, Mod1.pin_4
  N4: LED1.green_anode, Mod1.pin_6
  N5: LED1.blue_anode, Mod1.pin_9
  N6: Mod1.pin_3, Mod1.pin_8, Mod1.pin_13, Mod1.pin_18, Mod1.pin_23, Mod1.pin_28, Mod1.pin_33, Mod1.pin_38

custom parts:
  Raspberry Pi Pico: Raspberry Pi Pico. Based around the RP2040 microcontroller the Pico is a low cost microcontroller device bringing Raspberry Pi quality, cost, and easy of use to the microcontroller space. Jan 2021, Split part in to two versions: tht (this one) and SMD. This one will drill holes for a .1 in header in pcb to allow plugging in the module as well as providing pads to solder the module to the top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
