# Fritzing sketch p4 (saved by Fritzing 0.9.4)
breadboards: 1

parts:
  LED1 = smd LED [color="Green (555nm)" package="1206 [SMD]"]
  Mod1 = Raspberry Pi Pico
  LED2 = smd LED [color="Green (555nm)" package="1206 [SMD]"]
  LED3 = smd LED [color="Green (555nm)" package="1206 [SMD]"]
  LED4 = smd LED [color="Green (555nm)" package="1206 [SMD]"]
  S2 = Pushbutton [package="[THT]"]
  S3 = Pushbutton [package="[THT]"]
  R1 = Resistor [tolerance=±5% resistance=220 package=THT]

nets:
  N1: LED1.cathode, LED2.cathode, LED3.cathode, LED4.cathode, R1.Pin_0
  N2: LED1.anode, Mod1.pin_1
  N3: Mod1.pin_2, LED2.anode
  N4: Mod1.pin_3, Mod1.pin_8, Mod1.pin_13, Mod1.pin_18, Mod1.pin_23, Mod1.pin_28, Mod1.pin_33, Mod1.pin_38, Mod1.pin_42, S2.Pin_3, S2.Pin_4, S3.Pin_3, S3.Pin_4, R1.Pin_1
  N5: Mod1.pin_4, LED3.anode
  N6: Mod1.pin_5, LED4.anode
  N7: Mod1.pin_31, S3.Pin_1, S3.Pin_2
  N8: Mod1.pin_32, S2.Pin_1, S2.Pin_2

custom parts:
  Raspberry Pi Pico: Raspberry Pi Pico. Based around the RP2040 microcontroller the Pico is a low cost microcontroller device bringing Raspberry Pi quality, cost, and easy of use to the microcontroller space. Jan 2021, Split part in to two versions: tht (this one) and SMD. This one will drill holes for a .1 in header in pcb to allow plugging in the module as well as providing pads to solder the module to the top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
