# Fritzing sketch p5 (saved by Fritzing 0.9.4)
breadboards: 1

parts:
  Mod1 = Raspberry Pi Pico
  DI1 = 7-Segment LED Display [package=THT]
  R1 = Resistor [tolerance=±5% resistance=220 package=THT]  # not connected

nets:
  N1: Mod1.pin_1, DI1.cathodeG
  N2: Mod1.pin_2, DI1.cathodeF
  N3: Mod1.pin_3, Mod1.pin_8, Mod1.pin_13, Mod1.pin_18, Mod1.pin_23, Mod1.pin_28, Mod1.pin_33, Mod1.pin_38, DI1.commAnode#2
  N4: Mod1.pin_4, DI1.cathodeA
  N5: Mod1.pin_5, DI1.cathodeB
  N6: Mod1.pin_6, DI1.cathodeE
  N7: Mod1.pin_7, DI1.cathodeD
  N8: Mod1.pin_9, DI1.cathodeC

custom parts:
  Raspberry Pi Pico: Raspberry Pi Pico. Based around the RP2040 microcontroller the Pico is a low cost microcontroller device bringing Raspberry Pi quality, cost, and easy of use to the microcontroller space. Jan 2021, Split part in to two versions: tht (this one) and SMD. This one will drill holes for a .1 in header in pcb to allow plugging in the module as well as providing pads to solder the module to the top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
