# Fritzing sketch p6 (saved by Fritzing 0.9.4)
breadboards: 1

parts:
  Mod1 = Raspberry Pi Pico
  U2 = LCD-16X2 [package=lcd-16x2]
  U3 = POT [package=pot_alpha_rv16af-20]

nets:
  N1: Mod1.pin_3, Mod1.pin_8, Mod1.pin_13, Mod1.pin_18, Mod1.pin_23, Mod1.pin_28, Mod1.pin_33, Mod1.pin_38, U2.VSS, U2.R_W, U2.K, U3.A
  N2: Mod1.pin_21, U2.RS
  N3: Mod1.pin_22, U2.E
  N4: Mod1.pin_24, U2.DB4
  N5: Mod1.pin_25, U2.DB5
  N6: Mod1.pin_26, U2.DB6
  N7: Mod1.pin_27, U2.DB7
  N8: Mod1.pin_36, U2.VDD, U2.A, U3.E
  N9: U2.VO, U3.S

custom parts:
  Raspberry Pi Pico: Raspberry Pi Pico. Based around the RP2040 microcontroller the Pico is a low cost microcontroller device bringing Raspberry Pi quality, cost, and easy of use to the microcontroller space. Jan 2021, Split part in to two versions: tht (this one) and SMD. This one will drill holes for a .1 in header in pcb to allow plugging in the module as well as providing pads to solder the module to the top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
