# Fritzing sketch p1 (saved by Fritzing 0.9.4)
breadboards: 1

parts:
  U1 = ESP32-38PinWide [part_number=ESP32-38PinWide]
  Part2 = Triple Axis Accelerometer Breakout - ADXL345
  J1 = Piezo Speaker
  LED2 = RGB LED - (4 legs) [package="5 mm [THT]"]

nets:
  GND: U1.GND, Part2.GND, J1.pin1
  N1: U1.GPIO4, LED2.red_cathode
  N2: U1.GPIO17, J1.pin2
  N3: U1.GPIO5, LED2.green_cathode
  N4: U1.GPIO18, LED2.blue_cathode
  N5: U1.GPIO19, LED2.common_anode
  N6: U1.GPIO21, Part2.SDA
  N7: U1.GPIO22, Part2.SCL
  N8: U1.GPIO23, Part2.VCC

custom parts:
  ESP32-38PinWide: Generic 38-Pin ESP32 with wide format (only access to one side of pins on a breadboard) based on Stephen Lilley's HiLetgo ESP-WROOM-32 ESP32 ESP-32S Development Board.
