# Fritzing sketch p2 (saved by Fritzing 0.9.4)
breadboards: 1

parts:
  U1 = ESP32-38PinWide [part_number=ESP32-38PinWide]
  LED6 = RGB LED - (4 legs) [package="5 mm [THT]"]

nets:
  N1: U1.3.3, LED6.common_anode
  N2: U1.GPIO15, LED6.red_cathode
  N3: U1.GPIO2, LED6.green_cathode
  N4: U1.GPIO0, LED6.blue_cathode

custom parts:
  ESP32-38PinWide: Generic 38-Pin ESP32 with wide format (only access to one side of pins on a breadboard) based on Stephen Lilley's HiLetgo ESP-WROOM-32 ESP32 ESP-32S Development Board.
