# Fritzing sketch p3 (saved by Fritzing 0.9.4)
breadboards: 1

parts:
  U1 = ESP32-38PinWide [part_number=ESP32-38PinWide]
  IC1 = L293D [package=THT]
  LED1 = LED - 5mm [color="Green (555nm)" package="5 mm [THT]"]
  Power_plug1 = Power plug
  LED2 = LED - 5mm [color="Green (555nm)" package="5 mm [THT]"]
  LED3 = LED - 5mm [color="Green (555nm)" package="5 mm [THT]"]
  LED4 = LED - 5mm [color="Green (555nm)" package="5 mm [THT]"]
  M1 = DC Motor
  Part3 = Triple Axis Accelerometer Breakout - ADXL345

nets:
  N1: U1.3.3, Part3.VCC
  N2: U1.GND, LED1.cathode, LED2.cathode, LED3.cathode, LED4.cathode
  N3: U1.GPIO15, LED1.anode
  N4: U1.GPIO2, LED2.anode
  N5: U1.GPIO0, LED3.anode
  N6: U1.GPIO4, LED4.anode
  N7: U1.GPIO18, IC1.In_4
  N8: U1.GPIO19, IC1.In_3
  N9: U1.GPIO21, Part3.SDA
  N10: U1.GPIO22, Part3.SCL
  N11: U1.GPIO23, IC1.Enable_2
  N12: IC1.0V, Power_plug1.GND, M1.pin_2
  N13: IC1.+Vmotor, IC1.+V, Power_plug1.VCC
  N14: IC1.Out_4_(_Controlled_by_Enable_2_), M1.pin_1

custom parts:
  ESP32-38PinWide: Generic 38-Pin ESP32 with wide format (only access to one side of pins on a breadboard) based on Stephen Lilley's HiLetgo ESP-WROOM-32 ESP32 ESP-32S Development Board.
